// Digital circuit address.dig as structural Verilog
module address (
  input  A7,
  input  A8,
  input  A9,
  input  A10,
  input  A11,
  input  A12,
  input  A13,
  input  A14,
  input  A15,
  input  A16,
  input  A17,
  input  A18,
  input  A19,
  input  A20,
  input  A21,
  input  A22,
  input  A23,
  output nRAM_EXT,
  output nROM,
  output nIO,
  output nRAM
);

  wire nand_1_out, nor_1_out, nor_2_out, nor_3_out, nor_4_out;

  nand nand_1 (nand_1_out, A14, A13, A12, A11, A10, A9, A8, A7);
  nor nor_1 (nor_1_out, A23, A22);
  nor nor_2 (nor_2_out, A21, A20);
  nor nor_3 (nor_3_out, A23, A22, A21, A20, A19, A18, A17, A16);
  nor nor_4 (nor_4_out, A15, 1'b0);
  nand nand_2 (nRAM_EXT, A19, nor_1_out, nor_2_out);
  nand nand_3 (nROM, nor_3_out, 1'b1, A15);
  nand nand_4 (nIO, nor_3_out, ~A15, ~nand_1_out);  // NAnd
  nand nand_5 (nRAM, nor_3_out, nor_4_out, nand_1_out);

  // Notes on the sheet:
  //   11; 44.5
  //   10; 30
  //   HC30
  //   HC02
  //   HC4078
  //   11; 67.5
  //   11; 68.5
  //   10; 53
  //   AC10
  //   AC138
  //   12; 75.5
  //   12; 76.5
  //   12.6; 78.5
  //   (12.8; 40 for select bits A4-A6)
  //   11; 76.5
  //   Worst case 78.5ns for I/O chip select
  //   Needs to happen 10ns 
  //   before rising edge of clock for 65C22
  //   => half-period of clock >= 88.5ns
  //   => period of clock >= 177ns
  //   => frequency <= 5.6MHz
  //   HC02: 0; 23
  //   HC30: 0; 23
  //   HC4078: 0: 24
  //   AC10: 1; 8
  //   AC138 act high: 2.8; 10 
  //   AC138 act low: 2.6; 9.1
  //   AC138 select: 2.8; 10
endmodule

/* Test case:
A23 A22 A21 A20 A19 A18 A17 A16 A15 A14 A13 A12 A11 A10 A9 A8 A7   ~ROM ~RAM ~RAM_EXT ~IO
1   X   X   X   X   X   X   X   X   X   X   X   X   X   X  X  X    1    1     1     1
0   1   X   X   X   X   X   X   X   X   X   X   X   X   X  X  X    1    1     1     1
0   0   1   X   X   X   X   X   X   X   X   X   X   X   X  X  X    1    1     1     1
0   0   0   1   X   X   X   X   X   X   X   X   X   X   X  X  X    1    1     1     1
0   0   0   0   1   X   X   X   X   X   X   X   X   X   X  X  X    1    1     0     1
0   0   0   0   0   1   X   X   X   X   X   X   X   X   X  X  X    1    1     1     1
0   0   0   0   0   0   1   X   X   X   X   X   X   X   X  X  X    1    1     1     1
0   0   0   0   0   0   0   1   X   X   X   X   X   X   X  X  X    1    1     1     1
0   0   0   0   0   0   0   0   1   X   X   X   X   X   X  X  X    0    1     1     1
0   0   0   0   0   0   0   0   0   1   1   1   1   1   1  1  1    1    1     1     0
0   0   0   0   0   0   0   0   0   1   1   1   1   1   1  1  0    1    0     1     1
0   0   0   0   0   0   0   0   0   1   1   1   1   1   1  0  X    1    0     1     1
0   0   0   0   0   0   0   0   0   1   1   1   1   1   0  X  X    1    0     1     1
0   0   0   0   0   0   0   0   0   1   1   1   1   0   X  X  X    1    0     1     1
0   0   0   0   0   0   0   0   0   1   1   1   0   X   X  X  X    1    0     1     1
0   0   0   0   0   0   0   0   0   1   1   0   X   X   X  X  X    1    0     1     1
0   0   0   0   0   0   0   0   0   1   0   X   X   X   X  X  X    1    0     1     1
0   0   0   0   0   0   0   0   0   0   X   X   X   X   X  X  X    1    0     1     1
*/
